# Fritzing sketch hardware (saved by Fritzing 0.9.3b)
breadboards: 1

parts:
  Part1 = Intel Edison Arduinobreakout
  Part2 = INA219 High Side DC Current Sensor Breakout [part_number=904]
  Q1 = Basic FET N-Channel [package="D2Pak [SMD]"]
  Part3 = Solar Cell
  R1 = Resistor [tolerance=±5% resistance=220 package="0402 [SMD]"]

nets:
  N1: Part1.A0, Q1.Gate, R1.Pin_0
  N2: Part1.A1, Part2.VIN+, Part3.+
  N3: Part1.A4/SDA, Part2.SDA, Part2.VIN-, Q1.drain
  N4: Part1.A5/SCL, Part2.SCL
  5V: Part1.5V, Part2.VCC
  GND: Part1.GND, Part2.GND, Q1.source, Part3.-, R1.Pin_1

custom parts:
  INA219 High Side DC Current Sensor Breakout: This breakout board will solve all your power-monitoring problems. Instead of struggling with two multimeters, you can just use the handy INA219B chip on this breakout to both measure both the high side voltage and DC current draw over I2C with 1% precision. Most current-measuring devices such as our current panel meter are only good for low side measuring. That means that unless you want to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
